// Logisim project Computer.circ as structural Verilog: 1 circuit, main circuit main
module main (
);

  wire and_1_out, and_2_out, and_3_out, BR, CLK, EZ_ACC, GZ_ACC, LZ_ACC, N, or_2_out, P, Z;
  wire [3:0] bit_extender_1_out, Output_q, Output_q_2;
  wire [7:0] ACC_q, adder_1_out, adder_2_out, B_q, bit_extender_2_out, BUS, controlled_buffer_1_out,
       controlled_buffer_4_out, controlled_buffer_6_out, controlled_buffer_9_out, controlled_buffer_10_out,
       controlled_buffer_13_out, controlled_buffer_14_out, MAR_q, multiplexer_1_out, PC_q, ram_1_data,
       subtractor_1_out;
  wire [7:3] IR_q;

  and and_1 (and_1_out, P, GZ_ACC);
  and and_2 (and_2_out, Z, EZ_ACC);
  and and_3 (and_3_out, N, LZ_ACC);
  Register IR (.D(controlled_buffer_9_out), .en(1'b0), .Q({IR_q, N, Z, P}), .clk(CLK));  // open: clr
  or or_1 (BR, and_1_out, and_2_out, and_3_out);
  Adder adder_1 (.a(8'h1), .b(PC_q), .out(adder_1_out));  // open: cin, cout
  assign controlled_buffer_1_out = 1'b0 ? adder_1_out : 8'bz;  // Controlled_Buffer controlled_buffer_1
  Register PC (.D(controlled_buffer_1_out), .en(or_2_out), .Q(PC_q), .clk(CLK));  // open: clr
  or or_2 (or_2_out, 1'b0, 1'b0);
  Register MAR (.D(controlled_buffer_4_out), .en(1'b0), .Q(MAR_q), .clk(CLK));  // open: clr
  Bit_Extender #(.out_width(4)) bit_extender_1 (.in({IR_q, N, Z, P}), .out(bit_extender_1_out));
  assign BUS = 1'b0 ? PC_q : 8'bz;  // Controlled_Buffer controlled_buffer_2
  assign controlled_buffer_1_out = 1'b0 ? BUS : 8'bz;  // Controlled_Buffer controlled_buffer_3
  assign controlled_buffer_4_out = 1'b0 ? BUS : 8'bz;  // Controlled_Buffer controlled_buffer_4
  RAM #(.bus("separate")) ram_1 (
    .addr(MAR_q), .din(controlled_buffer_6_out), .data(ram_1_data), .str(1'b0), .sel(1'b1), .clk(CLK),
    .ld(1'b0));  // open: clr
  assign BUS = 1'b0 ? ram_1_data : 8'bz;  // Controlled_Buffer controlled_buffer_5
  assign controlled_buffer_6_out = 1'b0 ? BUS : 8'bz;  // Controlled_Buffer controlled_buffer_6
  assign BUS = 1'b0 ? {IR_q, N, Z, P} : 8'bz;  // Controlled_Buffer controlled_buffer_7
  assign BUS = 1'b0 ? bit_extender_2_out : 8'bz;  // Controlled_Buffer controlled_buffer_8
  assign bit_extender_2_out = {{4{bit_extender_1_out[3]}}, bit_extender_1_out};  // Bit_Extender bit_extender_2
  assign controlled_buffer_9_out = 1'b0 ? BUS : 8'bz;  // Controlled_Buffer controlled_buffer_9
  LED led_1 (.in(CLK));
  DotMatrix #(.matrixcols(8), .matrixrows(1)) dotmatrix_1 (
    .col0(BUS[7]), .col1(BUS[6]), .col2(BUS[5]), .col3(BUS[4]), .col4(BUS[3]), .col5(BUS[2]), .col6(BUS[1]),
    .col7(BUS[0]));
  assign controlled_buffer_10_out = 1'b0 ? BUS : 8'bz;  // Controlled_Buffer controlled_buffer_10
  assign BUS = 1'b0 ? ACC_q : 8'bz;  // Controlled_Buffer controlled_buffer_11
  assign BUS = 1'b0 ? multiplexer_1_out : 8'bz;  // Controlled_Buffer controlled_buffer_12
  assign controlled_buffer_13_out = 1'b0 ? BUS : 8'bz;  // Controlled_Buffer controlled_buffer_13
  assign controlled_buffer_14_out = 1'b0 ? BUS : 8'bz;  // Controlled_Buffer controlled_buffer_14
  Register ACC (.D(controlled_buffer_10_out), .en(1'b0), .Q(ACC_q), .clk(CLK));  // open: clr
  Register B (.D(controlled_buffer_13_out), .en(1'b0), .Q(B_q), .clk(CLK));  // open: clr
  Register Output (.D(controlled_buffer_14_out), .en(1'b0), .Q({Output_q_2, Output_q}), .clk(CLK));  // open: clr
  Hex_Digit_Display hex_digit_display_1 (.value(Output_q));  // open: dp
  Hex_Digit_Display hex_digit_display_2 (.value(Output_q_2));  // open: dp
  Comparator comparator_1 (.a(ACC_q), .b({8{1'b0}}), .gt(GZ_ACC), .eq(EZ_ACC), .lt(LZ_ACC));
  Adder adder_2 (.a(ACC_q), .b(B_q), .out(adder_2_out));  // open: cin, cout
  Multiplexer #(.width(8), .enable("false")) multiplexer_1 (
    .in0(adder_2_out), .in1(subtractor_1_out), .out(multiplexer_1_out), .sel(1'b0));
  Subtractor subtractor_1 (.a(ACC_q), .b(B_q), .out(subtractor_1_out));  // open: bin, bout
  Clock clock_1 (.out(CLK));

  // Notes on the sheet:
  //   Memory
  //   IR
  //   PC
  //   CONTROL
  //   ACC
  //   OR
  //   B
  //   ALU
endmodule
